// Logisim project 16bitGPU3.circ as structural Verilog: 2 circuits, main circuit multicore
module singlecore (
  input  [47:0] A_IN,
  input  [47:0] B_IN,
  input  STR,
  input  RST,
  input  [15:0] FOV,
  output [7:0] LN_CNT,
  output Finished,
  output RST_OUT,
  output CLK,
  output WE,
  output [5:0] X_OUT,
  output [5:0] Y_OUT,
  output [23:0] RGB
);

  wire and_1_out, and_2_out, and_3_out, and_4_out, and_5_out, and_6_out, and_7_out, and_8_out, and_9_out,
       and_10_out, and_12_out, and_13_out, and_14_out, and_15_out, and_16_out, and_17_out, clock_2_out,
       clock_3_out, clock_4_out, clock_5_out, comparator_1_eq, comparator_1_gt, comparator_1_lt,
       comparator_2_lt, comparator_3_gt, comparator_4_gt, comparator_5_lt, comparator_6_eq, comparator_7_eq,
       comparator_8_lt, comparator_9_eq, comparator_10_eq, comparator_11_eq, comparator_11_gt,
       comparator_11_lt, comparator_12_eq, comparator_13_eq, comparator_14_eq, comparator_14_gt,
       comparator_14_lt, comparator_15_eq, comparator_16_eq, comparator_17_lt, comparator_18_eq,
       comparator_19_eq, multiplexer_23_out, multiplexer_39_out, not_1_out, not_2_out, not_3_out, not_4_out,
       not_5_out, not_6_out, not_7_out, or_1_out, or_2_out, or_3_out, or_4_out, register_1_q, register_2_q,
       register_3_q, register_4_q, register_5_q, register_6_q, xor_1_out, xor_2_out, xor_3_out, xor_4_out,
       xor_5_out, xor_6_out;
  wire [4:1] rom_2_data;
  wire [5:0] X_q, X_SUB_q, Y_CNT_q;
  wire [7:0] counter_3_q;
  wire [8:0] counter_2_q, counter_4_q;
  wire [15:0] adder_1_out, adder_2_out, adder_3_out, adder_4_out, adder_5_out, adder_6_out, adder_7_out,
       adder_8_out, adder_9_out, adder_10_out, D2_q, D2_SUB_q, D_q, D_Sub_q, divider_1_out, divider_2_out,
       divider_3_out, divider_4_out, DX2_p1, DX_p1, DX_REG_q, DY2_p1, DY_p1, DY_REG_q, multiplexer_1_out,
       multiplexer_2_out, multiplexer_3_out, multiplexer_4_out, multiplexer_5_out, multiplexer_6_out,
       multiplexer_7_out, multiplexer_8_out, multiplexer_9_out, multiplexer_10_out, multiplexer_11_out,
       multiplexer_12_out, multiplexer_13_out, multiplexer_14_out, multiplexer_15_out, multiplexer_16_out,
       multiplexer_17_out, multiplexer_24_out, multiplexer_25_out, multiplexer_26_out, multiplexer_27_out,
       multiplexer_28_out, multiplexer_29_out, multiplexer_30_out, multiplexer_31_out, multiplexer_32_out,
       multiplexer_33_out, multiplexer_34_out, multiplexer_35_out, multiplexer_36_out, multiplexer_37_out,
       multiplexer_38_out, multiplier_1_out, multiplier_2_out, multiplier_3_out, multiplier_4_out,
       multiplier_5_out, multiplier_6_out, multiplier_7_out, multiplier_8_out, multiplier_9_out,
       multiplier_10_out, negator_1_out, negator_2_out, subtractor_1_out, subtractor_3_out, subtractor_4_out,
       subtractor_6_out, subtractor_7_out, subtractor_10_out, XI_q, XREG_q, Y_q, Y_sub_q, YI_q;
  wire [15:6] X_q_2, X_SUB_q_2, Y_CNT_q_2;
  wire [16:0] rom_1_data, rom_3_data;

  Subtractor #(.width(16)) subtractor_1 (
    .a(divider_3_out), .b(divider_1_out), .out(subtractor_1_out));  // open: bin, bout
  // LedBar #(.inputtype("row"), .matrixcols(16)) DX: pin names not known; wires that end beside it: DX_p1
  Multiplexer #(.width(16)) multiplexer_1 (
    .in0(divider_1_out), .in1(divider_3_out), .out(multiplexer_1_out), .sel(and_7_out));
  Multiplexer #(.width(16)) multiplexer_2 (
    .in0(divider_2_out), .in1(divider_4_out), .out(multiplexer_2_out), .sel(and_7_out));
  Multiplexer #(.width(16)) multiplexer_3 (
    .in0(divider_3_out), .in1(divider_1_out), .out(multiplexer_3_out), .sel(and_7_out));
  Multiplexer #(.width(16)) multiplexer_4 (
    .in0(divider_4_out), .in1(divider_2_out), .out(multiplexer_4_out), .sel(and_7_out));
  Subtractor #(.width(16)) subtractor_2 (
    .a(multiplexer_11_out), .b(multiplexer_5_out), .out(DX_p1));  // open: bin, bout
  Negator #(.width(16)) negator_1 (.in(DY_p1), .out(negator_1_out));
  Subtractor #(.width(16)) subtractor_3 (.a(DY_REG_q), .b(DX_p1), .out(subtractor_3_out));  // open: bin, bout
  Multiplier #(.mode("twosComplement"), .width(16)) multiplier_1 (
    .a(subtractor_3_out), .b(16'h2), .out(multiplier_1_out));  // open: cin, cout
  Adder #(.width(16)) adder_1 (.a(multiplier_1_out), .b(D_Sub_q), .out(adder_1_out));  // open: cin, cout
  Adder #(.width(16)) adder_2 (.a(D_Sub_q), .b(multiplier_5_out), .out(adder_2_out));  // open: cin, cout
  Comparator #(.width(16)) comparator_1 (
    .a(D_Sub_q), .b({16{1'b0}}), .gt(comparator_1_gt), .eq(comparator_1_eq), .lt(comparator_1_lt));
  Multiplier #(.mode("twosComplement"), .width(16)) multiplier_2 (
    .a(FOV), .b(A_IN[15:0]), .out(multiplier_2_out));  // open: cin, cout
  Adder #(.width(16)) adder_3 (.a(FOV), .b(A_IN[47:32]), .out(adder_3_out));  // open: cin, cout
  Multiplier #(.mode("twosComplement"), .width(16)) multiplier_3 (
    .a(A_IN[31:16]), .b(FOV), .out(multiplier_3_out));  // open: cin, cout
  Adder #(.width(16)) adder_4 (.a(A_IN[47:32]), .b(FOV), .out(adder_4_out));  // open: cin, cout
  Comparator #(.width(16)) comparator_2 (.a(subtractor_1_out), .b({16{1'b0}}), .lt(comparator_2_lt));  // open: gt, eq
  Multiplexer #(.width(16)) multiplexer_5 (
    .in0({16{1'b0}}), .in1(multiplexer_1_out), .out(multiplexer_5_out), .sel(rom_2_data[4]));
  Multiplexer #(.width(16)) multiplexer_6 (.in0(DY_p1), .in1(negator_1_out), .out(multiplexer_6_out), .sel(and_3_out));
  Multiplexer #(.width(16)) multiplexer_7 (
    .in0(D_Sub_q), .in1(adder_1_out), .out(multiplexer_7_out), .sel(register_1_q));
  Adder #(.width(16)) adder_5 (.a(Y_sub_q), .b(YI_q), .out(adder_5_out));  // open: cin, cout
  Register #(.width(1)) register_1 (.D(comparator_1_gt), .en(1'b1), .clk(CLK), .Q(register_1_q), .clr(and_10_out));
  Register #(.width(1)) register_2 (.D(comparator_1_eq), .en(1'b1), .clk(CLK), .Q(register_2_q), .clr(and_10_out));
  Register #(.width(1)) register_3 (.D(comparator_1_lt), .en(1'b1), .clk(CLK), .Q(register_3_q), .clr(and_10_out));
  Divider #(.mode("twosComplement"), .width(16)) divider_1 (
    .a(multiplier_2_out), .b(adder_3_out), .out(divider_1_out));  // open: upper, rem
  Divider #(.mode("twosComplement"), .width(16)) divider_2 (
    .a(multiplier_3_out), .b(adder_4_out), .out(divider_2_out));  // open: upper, rem
  Subtractor #(.width(16)) subtractor_4 (
    .a(divider_4_out), .b(divider_2_out), .out(subtractor_4_out));  // open: bin, bout
  Multiplier #(.mode("twosComplement"), .width(16)) multiplier_4 (
    .a(subtractor_1_out), .b(multiplexer_8_out), .out(multiplier_4_out));  // open: cin, cout
  Multiplexer #(.width(16)) multiplexer_8 (
    .in0(16'h1), .in1({16{1'b1}}), .out(multiplexer_8_out), .sel(comparator_2_lt));
  Comparator #(.width(16)) comparator_3 (.a(divider_1_out), .b(divider_3_out), .gt(comparator_3_gt));  // open: eq, lt
  Comparator #(.width(16)) comparator_4 (.a(divider_2_out), .b(divider_4_out), .gt(comparator_4_gt));  // open: eq, lt
  Multiplexer #(.width(16)) multiplexer_9 (
    .in0({16{1'b0}}), .in1(multiplexer_2_out), .out(multiplexer_9_out), .sel(rom_2_data[4]));
  // LedBar #(.inputtype("row"), .matrixcols(16)) DY: pin names not known; wires that end beside it: DY_p1
  Comparator #(.width(16)) comparator_5 (.a(DY_p1), .b({16{1'b0}}), .lt(comparator_5_lt));  // open: gt, eq
  Register #(.width(16)) DY_REG (.D(multiplexer_6_out), .en(rom_1_data[3]), .clk(CLK), .Q(DY_REG_q));  // open: clr
  Multiplier #(.mode("twosComplement"), .width(16)) multiplier_5 (
    .a(DY_REG_q), .b(16'h2), .out(multiplier_5_out));  // open: cin, cout
  Multiplexer #(.width(16)) multiplexer_10 (
    .in0(Y_sub_q), .in1(adder_5_out), .out(multiplexer_10_out), .sel(and_1_out));
  and and_1 (and_1_out, rom_1_data[12], register_1_q);
  Comparator #(.width(16)) comparator_6 (.a(divider_1_out), .b({16{1'b0}}), .eq(comparator_6_eq));  // open: gt, lt
  Comparator #(.width(16)) comparator_7 (.a(divider_2_out), .b({16{1'b0}}), .eq(comparator_7_eq));  // open: gt, lt
  Multiplexer #(.width(16)) multiplexer_11 (
    .in0({16{1'b0}}), .in1(multiplexer_3_out), .out(multiplexer_11_out), .sel(rom_2_data[4]));
  Multiplexer #(.width(16)) multiplexer_12 (
    .in0({16{1'b0}}), .in1(multiplexer_4_out), .out(multiplexer_12_out), .sel(rom_2_data[4]));
  Subtractor #(.width(16)) subtractor_5 (
    .a(multiplexer_12_out), .b(multiplexer_9_out), .out(DY_p1));  // open: bin, bout
  and and_2 (and_2_out, rom_1_data[2], comparator_5_lt);
  and and_3 (and_3_out, comparator_5_lt, rom_1_data[4]);
  Subtractor #(.width(16)) subtractor_6 (.a(multiplier_5_out), .b(DX_p1), .out(subtractor_6_out));  // open: bin, bout
  Multiplexer #(.width(16)) multiplexer_13 (
    .in0(multiplexer_7_out), .in1(multiplexer_14_out), .out(multiplexer_13_out), .sel(rom_1_data[16]));
  Multiplexer #(.width(16)) multiplexer_14 (.in0(D_q), .in1(adder_2_out), .out(multiplexer_14_out), .sel(or_1_out));
  or or_1 (or_1_out, register_2_q, register_3_q);
  Comparator #(.width(16)) comparator_8 (.a(subtractor_4_out), .b({16{1'b0}}), .lt(comparator_8_lt));  // open: gt, eq
  Multiplexer #(.width(16)) multiplexer_15 (
    .in0(16'h1), .in1({16{1'b1}}), .out(multiplexer_15_out), .sel(comparator_8_lt));
  or or_2 (or_2_out, comparator_11_gt, comparator_11_eq);
  and and_4 (and_4_out, or_2_out, comparator_4_gt);
  and and_5 (and_5_out, comparator_6_eq, comparator_7_eq);
  Comparator #(.width(16)) comparator_9 (.a(divider_3_out), .b({16{1'b0}}), .eq(comparator_9_eq));  // open: gt, lt
  and and_6 (and_6_out, comparator_9_eq, comparator_10_eq);
  Comparator #(.width(16)) comparator_10 (.a(divider_4_out), .b({16{1'b0}}), .eq(comparator_10_eq));  // open: gt, lt
  Multiplexer #(.width(16)) multiplexer_16 (
    .in0(subtractor_6_out), .in1(multiplexer_13_out), .out(multiplexer_16_out), .sel(rom_1_data[15]));
  Multiplexer #(.width(16)) multiplexer_17 (
    .in0(multiplexer_9_out), .in1(multiplexer_10_out), .out(multiplexer_17_out), .sel(rom_1_data[12]));
  Multiplier #(.mode("twosComplement"), .width(16)) multiplier_6 (
    .a(FOV), .b(B_IN[15:0]), .out(multiplier_6_out));  // open: cin, cout
  Adder #(.width(16)) adder_6 (.a(FOV), .b(B_IN[47:32]), .out(adder_6_out));  // open: cin, cout
  Multiplier #(.mode("twosComplement"), .width(16)) multiplier_7 (
    .a(B_IN[31:16]), .b(FOV), .out(multiplier_7_out));  // open: cin, cout
  Adder #(.width(16)) adder_7 (.a(B_IN[47:32]), .b(FOV), .out(adder_7_out));  // open: cin, cout
  Multiplier #(.mode("twosComplement"), .width(16)) multiplier_8 (
    .a(subtractor_4_out), .b(multiplexer_15_out), .out(multiplier_8_out));  // open: cin, cout
  Comparator #(.width(16)) comparator_11 (
    .a(multiplier_8_out), .b(multiplier_4_out), .gt(comparator_11_gt), .eq(comparator_11_eq),
    .lt(comparator_11_lt));
  and and_7 (and_7_out, or_3_out, comparator_3_gt);
  and and_8 (and_8_out, and_5_out, and_6_out);
  Counter #(.max('hffff), .width(16)) YI (
    .clr(rom_1_data[1]), .up(not_1_out), .clk(xor_1_out), .Q(YI_q));  // open: load, count, D, carry
  not not_1 (not_1_out, and_2_out);
  Register #(.width(16)) D (.D(multiplexer_16_out), .en(rom_1_data[5]), .clk(CLK), .Q(D_q));  // open: clr
  Register #(.width(16)) Y (.D(multiplexer_17_out), .en(and_9_out), .clk(CLK), .Q(Y_q));  // open: clr
  and and_9 (and_9_out, rom_1_data[11], not_3_out);
  Divider #(.mode("twosComplement"), .width(16)) divider_3 (
    .a(multiplier_6_out), .b(adder_6_out), .out(divider_3_out));  // open: upper, rem
  Divider #(.mode("twosComplement"), .width(16)) divider_4 (
    .a(multiplier_7_out), .b(adder_7_out), .out(divider_4_out));  // open: upper, rem
  or or_3 (or_3_out, comparator_11_eq, comparator_11_lt);
  not not_2 (not_2_out, and_8_out);
  Register #(.width(16)) D_Sub (.D(D_q), .en(rom_1_data[14]), .clk(CLK), .Q(D_Sub_q));  // open: clr
  Register #(.width(16)) Y_sub (.D(Y_q), .en(rom_1_data[13]), .clk(CLK), .Q(Y_sub_q));  // open: clr
  Clock clock_1 (.out(CLK));
  xor xor_1 (xor_1_out, rom_1_data[0], and_2_out);
  not not_3 (not_3_out, comparator_12_eq);
  Comparator #(.width(16)) comparator_12 (.a(Y_sub_q), .b(multiplexer_12_out), .eq(comparator_12_eq));  // open: gt, lt
  and and_10 (and_10_out, rom_1_data[1], rom_1_data[10]);
  Multiplexer #(.enable("true"), .width(6)) multiplexer_18 (
    .in0(X_SUB_q), .in1(X_q), .out(X_OUT), .sel(or_3_out), .en(not_2_out));
  Multiplexer #(.enable("true"), .width(24)) multiplexer_19 (
    .in0({24{1'b1}}), .in1({24{1'b1}}), .out(RGB), .sel(or_3_out), .en(not_2_out));
  Multiplexer #(.enable("true"), .width(6)) multiplexer_20 (
    .in0(Y_CNT_q), .in1(Y_sub_q[5:0]), .out(Y_OUT), .sel(or_3_out), .en(not_2_out));
  Multiplexer #(.enable("true")) multiplexer_21 (
    .in0(rom_3_data[9]), .in1(rom_1_data[9]), .out(WE), .sel(or_3_out), .en(not_2_out));
  Multiplexer multiplexer_22 (.in0(rom_3_data[10]), .in1(rom_1_data[10]), .sel(or_3_out));  // open: out
  Counter #(.max('hffff), .width(16)) X (
    .clr(xor_2_out), .load(rom_1_data[8]), .count(not_4_out), .clk(rom_1_data[7]), .D(multiplexer_5_out),
    .Q({X_q_2, X_q}));  // open: up, carry
  LED led_1 (.in(register_1_q));
  buf xor_2 (xor_2_out, rom_1_data[6]);  // XOR_Gate
  LED led_2 (.in(or_1_out));
  Counter counter_1 (.clr(RST_OUT), .clk(rom_2_data[1]), .Q(LN_CNT));  // open: load, up, count, D, carry
  Comparator #(.width(16)) comparator_13 (
    .a(multiplexer_11_out), .b({X_q_2, X_q}), .eq(comparator_13_eq));  // open: gt, lt
  not not_4 (not_4_out, comparator_13_eq);
  Clock clock_2 (.out(clock_2_out));
  Counter #(.max('h1ff), .width(9)) counter_2 (
    .clr(rom_2_data[3]), .clk(multiplexer_23_out), .Q(counter_2_q));  // open: load, up, count, D, carry
  Multiplexer multiplexer_23 (.in1(clock_2_out), .out(multiplexer_23_out), .sel(xor_3_out));  // open: in0
  xor xor_3 (xor_3_out, rom_2_data[2], comparator_13_eq);
  ROM #(.addrWidth(9), .dataWidth(17)) rom_1 (.addr(counter_2_q), .data(rom_1_data));
  Multiplexer #(.width(16)) multiplexer_24 (
    .in0(divider_1_out), .in1(divider_3_out), .out(multiplexer_24_out), .sel(and_4_out));
  Multiplexer #(.width(16)) multiplexer_25 (
    .in0(divider_2_out), .in1(divider_4_out), .out(multiplexer_25_out), .sel(and_4_out));
  Multiplexer #(.width(16)) multiplexer_26 (
    .in0(divider_3_out), .in1(divider_1_out), .out(multiplexer_26_out), .sel(and_4_out));
  Multiplexer #(.width(16)) multiplexer_27 (
    .in0(divider_4_out), .in1(divider_2_out), .out(multiplexer_27_out), .sel(and_4_out));
  // LedBar #(.inputtype("row"), .matrixcols(16)) DX2: pin names not known; wires that end beside it: DX2_p1
  Subtractor #(.width(16)) subtractor_7 (.a(DX_REG_q), .b(DY2_p1), .out(subtractor_7_out));  // open: bin, bout
  Multiplier #(.mode("twosComplement"), .width(16)) multiplier_9 (
    .a(subtractor_7_out), .b(16'h2), .out(multiplier_9_out));  // open: cin, cout
  Adder #(.width(16)) adder_8 (.a(multiplier_9_out), .b(D2_SUB_q), .out(adder_8_out));  // open: cin, cout
  Adder #(.width(16)) adder_9 (.a(D2_SUB_q), .b(multiplier_10_out), .out(adder_9_out));  // open: cin, cout
  Multiplexer #(.width(16)) multiplexer_28 (
    .in0({16{1'b0}}), .in1(multiplexer_24_out), .out(multiplexer_28_out), .sel(rom_2_data[4]));
  Subtractor #(.width(16)) subtractor_8 (
    .a(multiplexer_32_out), .b(multiplexer_28_out), .out(DX2_p1));  // open: bin, bout
  Negator #(.width(16)) negator_2 (.in(DX2_p1), .out(negator_2_out));
  Comparator #(.width(16)) comparator_14 (
    .a(D2_SUB_q), .b({16{1'b0}}), .gt(comparator_14_gt), .eq(comparator_14_eq), .lt(comparator_14_lt));
  Register #(.width(1)) register_4 (
    .D(comparator_14_gt), .en(1'b1), .clk(clock_3_out), .Q(register_4_q), .clr(and_17_out));
  Register #(.width(1)) register_5 (
    .D(comparator_14_eq), .en(1'b1), .clk(clock_3_out), .Q(register_5_q), .clr(and_17_out));
  Register #(.width(1)) register_6 (
    .D(comparator_14_lt), .en(1'b1), .clk(clock_3_out), .Q(register_6_q), .clr(and_17_out));
  Comparator #(.width(48)) comparator_15 (.a(B_IN), .b({48{1'b0}}), .eq(comparator_15_eq));  // open: gt, lt
  and and_11 (Finished, comparator_15_eq, comparator_16_eq);
  Comparator #(.width(48)) comparator_16 (.a(A_IN), .b({48{1'b0}}), .eq(comparator_16_eq));  // open: gt, lt
  Multiplexer #(.width(16)) multiplexer_29 (
    .in0({16{1'b0}}), .in1(multiplexer_25_out), .out(multiplexer_29_out), .sel(rom_2_data[4]));
  // LedBar #(.inputtype("row"), .matrixcols(16)) DY2: pin names not known; wires that end beside it: DY2_p1
  Multiplexer #(.width(16)) multiplexer_30 (
    .in0(DX2_p1), .in1(negator_2_out), .out(multiplexer_30_out), .sel(and_14_out));
  Multiplexer #(.width(16)) multiplexer_31 (
    .in0(D2_SUB_q), .in1(adder_8_out), .out(multiplexer_31_out), .sel(register_4_q));
  Adder #(.width(16)) adder_10 (.a({X_SUB_q_2, X_SUB_q}), .b(XI_q), .out(adder_10_out));  // open: cin, cout
  Multiplexer #(.width(16)) multiplexer_32 (
    .in0({16{1'b0}}), .in1(multiplexer_26_out), .out(multiplexer_32_out), .sel(rom_2_data[4]));
  Subtractor #(.width(16)) subtractor_9 (
    .a(multiplexer_35_out), .b(multiplexer_29_out), .out(DY2_p1));  // open: bin, bout
  Comparator #(.width(16)) comparator_17 (.a(DX2_p1), .b({16{1'b0}}), .lt(comparator_17_lt));  // open: gt, eq
  Register #(.width(16)) DX_REG (
    .D(multiplexer_30_out), .en(rom_3_data[3]), .clk(clock_3_out), .Q(DX_REG_q));  // open: clr
  Multiplier #(.mode("twosComplement"), .width(16)) multiplier_10 (
    .a(DX_REG_q), .b(16'h2), .out(multiplier_10_out));  // open: cin, cout
  Multiplexer #(.width(16)) multiplexer_33 (.in0(D2_q), .in1(adder_9_out), .out(multiplexer_33_out), .sel(or_4_out));
  Multiplexer #(.width(16)) multiplexer_34 (
    .in0({X_SUB_q_2, X_SUB_q}), .in1(adder_10_out), .out(multiplexer_34_out), .sel(and_12_out));
  and and_12 (and_12_out, rom_3_data[12], register_4_q);
  or or_4 (or_4_out, register_5_q, register_6_q);
  Multiplexer #(.width(16)) multiplexer_35 (
    .in0({16{1'b0}}), .in1(multiplexer_27_out), .out(multiplexer_35_out), .sel(rom_2_data[4]));
  and and_13 (and_13_out, rom_3_data[2], comparator_17_lt);
  and and_14 (and_14_out, comparator_17_lt, rom_3_data[4]);
  Subtractor #(.width(16)) subtractor_10 (
    .a(multiplier_10_out), .b(DY2_p1), .out(subtractor_10_out));  // open: bin, bout
  Multiplexer #(.width(16)) multiplexer_36 (
    .in0(multiplexer_31_out), .in1(multiplexer_33_out), .out(multiplexer_36_out), .sel(rom_3_data[16]));
  Multiplexer #(.width(16)) multiplexer_37 (
    .in0(multiplexer_28_out), .in1(multiplexer_34_out), .out(multiplexer_37_out), .sel(rom_3_data[12]));
  not not_5 (not_5_out, and_13_out);
  Multiplexer #(.width(16)) multiplexer_38 (
    .in0(subtractor_10_out), .in1(multiplexer_36_out), .out(multiplexer_38_out), .sel(rom_3_data[15]));
  Register #(.width(16)) D2 (.D(multiplexer_38_out), .en(rom_3_data[5]), .clk(clock_3_out), .Q(D2_q));  // open: clr
  Register #(.width(16)) XREG (.D(multiplexer_37_out), .en(and_15_out), .clk(clock_3_out), .Q(XREG_q));  // open: clr
  and and_15 (and_15_out, rom_3_data[11], not_6_out);
  Counter #(.max('hffff), .width(16)) XI (
    .clr(rom_3_data[1]), .up(not_5_out), .clk(xor_4_out), .Q(XI_q));  // open: load, count, D, carry
  Clock clock_3 (.out(clock_3_out));
  xor xor_4 (xor_4_out, rom_3_data[0], and_13_out);
  Register #(.width(16)) D2_SUB (.D(D2_q), .en(rom_3_data[14]), .clk(clock_3_out), .Q(D2_SUB_q));  // open: clr
  Register #(.width(16)) X_SUB (
    .D(XREG_q), .en(rom_3_data[13]), .clk(clock_3_out), .Q({X_SUB_q_2, X_SUB_q}));  // open: clr
  Comparator #(.width(16)) comparator_18 (
    .a({X_SUB_q_2, X_SUB_q}), .b(multiplexer_35_out), .eq(comparator_18_eq));  // open: gt, lt
  Clock #(.highDuration(350), .lowDuration(350)) clock_4 (.out(clock_4_out));
  not not_6 (not_6_out, comparator_18_eq);
  and and_16 (and_16_out, STR, clock_4_out);
  and and_17 (and_17_out, rom_3_data[1], rom_3_data[10]);
  Counter counter_3 (.clr(RST), .clk(and_16_out), .Q(counter_3_q));  // open: load, up, count, D, carry
  LED led_3 (.in(register_4_q));
  buf xor_5 (xor_5_out, rom_3_data[6]);  // XOR_Gate
  Counter #(.max('hffff), .width(16)) Y_CNT (
    .clr(xor_5_out), .load(rom_3_data[8]), .count(not_7_out), .clk(rom_3_data[7]), .D(multiplexer_29_out),
    .Q({Y_CNT_q_2, Y_CNT_q}));  // open: up, carry
  LED led_4 (.in(or_4_out));
  ROM #(.dataWidth(5), .misaligned("true")) rom_2 (.addr(counter_3_q), .data({rom_2_data, RST_OUT}));
  Comparator #(.width(16)) comparator_19 (
    .a(multiplexer_35_out), .b({Y_CNT_q_2, Y_CNT_q}), .eq(comparator_19_eq));  // open: gt, lt
  not not_7 (not_7_out, comparator_19_eq);
  Multiplexer multiplexer_39 (.in1(clock_5_out), .out(multiplexer_39_out), .sel(xor_6_out));  // open: in0
  Clock clock_5 (.out(clock_5_out));
  xor xor_6 (xor_6_out, rom_2_data[2], comparator_19_eq);
  Counter #(.max('h1ff), .width(9)) counter_4 (
    .clr(rom_2_data[3]), .clk(multiplexer_39_out), .Q(counter_4_q));  // open: load, up, count, D, carry
  ROM #(.addrWidth(9), .dataWidth(17)) rom_3 (.addr(counter_4_q), .data(rom_3_data));

  // Notes on the sheet:
  //   A_IN: initial=0x1
  //   B_IN: initial=0x1
  //   RST: initial=0x1
  //   STR: initial=0x1
  //   x1
  //   y1
  //   x2
  //   y2
  //   x1
  //   y1
  //   x2
  //   B
  //   y2
  //   A
  //   17 - D+(2*(dy-dx)) D+2*dy
  //   1 - Pulse YI
  //   2 - YI CLR
  //   3 - DY < 0 yi--
  //   4 -DY STR
  //   5 - DY < 0 invert
  //   6 - D IN
  //   7 - X CLR
  //   8 - X UP
  //   9 - X LD
  //   10 - PLT
  //   11 - RST screen
  //   12 - Y IN
  //   13 - Y y1/yi
  //   14 - Y sub IN
  //   15 - D sub IN
  //   16 - D sub/d2
  //   D > 0
  //   ELSE
  //   A
  //   contents of rom_1 (hex, n*v repeats v):
  //   6c62 1 4 0 4 18 20 4000 800 2000 180 200 1800 2000 8020 18020 4000 80 200 1800 2000 8020 18020 4000
  //   80 200 1800 2000 8020 18020 4000 80 200 1800 2000 8020 18020 4000 80 200 1800 2000 8020 18020 4000
  //   80 200 1800 2000 8020 18020 4000 80 200 1800 2000 8020 18020 4000 80 200 1800 2000 8020 18020 4000
  //   80 200 1800 2000 8020 18020 4000 80 200 1800 2000 8020 18020 4000 80 200 1800 2000 8020 18020 4000
  //   80 200 1800 2000 8020 18020 4000 80 200 1800 2000 8020 18020 4000 80 200 1800 2000 8020 18020 4000
  //   80 200 1800 2000 8020 18020 4000 80 200 1800 2000 8020 18020 4000 80 200 1800 2000 8020 18020 4000
  //   80 200 1800 2000 8020 18020 4000 80 200 1800 2000 8020 18020 4000 80 200 1800 2000 8020 18020 4000
  //   80 200 1800 2000 8020 18020 4000 80 200 1800 2000 8020 18020 4000 80 200 1800 2000 8020 18020 4000
  //   80 200 1800 2000 8020 18020 4000 80 200 1800 2000 8020 18020 4000 80 200 1800 2000 8020 18020 4000
  //   80 200 1800 2000 8020 18020 4000 80 200 1800 2000 8020 18020 4000 80 200 1800 2000 8020 18020 4000
  //   80 200 1800 2000 8020 18020 4000 80 200 1800 2000 8020 18020 4000 80 200 1800 2000 8020 18020 4000
  //   80 200 1800 2000 8020 18020 4000 80 200 1800 2000 8020 18020 4000 80 200 1800 2000 8020 18020 4000
  //   80 200 1800 2000 8020 18020 4000 80 200 1800 2000 8020 18020 4000 80 200 1800 2000 8020 18020 4000
  //   80 200 1800 2000 8020 18020 4000 80 200 1800 2000 8020 18020 4000 80 200 1800 2000 8020 18020 4000
  //   80 200 1800 2000 8020 18020 4000 80 200 1800 2000 8020 18020 4000 80 200 1800 2000 8020 18020 4000
  //   80 200 1800 2000 8020 18020 4000 80 200 1800 2000 8020 18020 4000 80 200 1800 2000 8020 18020 4000
  //   80 200 1800 2000 8020 18020 4000 80 200 1800 2000 8020 18020 4000 80 200 1800 2000 8020 18020 4000
  //   80 200 1800 2000 8020 18020 4000 80 200 1800 2000 8020 18020 4000 80 200 1800 2000 8020 18020 4000
  //   80 200 1800 2000 8020 18020 4000 80 200 1800 2000 8020 18020 4000 80 200 1800 2000 8020 18020 4000
  //   80 200 1800 2000 8020 18020 4000 80 200 1800 2000 8020 18020 4000 80 200 1800 2000 8020 18020 4000
  //   80 200 1800 2000 8020 18020 4000 80 200 1800 2000 8020 18020 4000 80 200 1800 2000 8020 18020 4000
  //   80 200 1800 2000 8020 18020 4000 80 200 1800 2000 8020 18020 4000 80 200 1800 2000 8020 18020 4000
  //   80 200 1800 2000 8020 18020 4000 80 200 1800 2000 8020 18020 4000 80 200 1800 2000 8020 18020 4000
  //   80 200 1800 2000 8020 18020 4000 80 200 1800 2000 8020 18020 4000 80
  //   B
  //   x1
  //   y1
  //   x2
  //   y2
  //   x1
  //   y1
  //   x2
  //   y2
  //   1 - RST LN_CNT + SCRN
  //   2- Pulse LN_CNT
  //   3 - 1 Starts CLK
  //   4 - 1 RSTS counters
  //   5 - 1 to input values
  //   1
  //   17 - D+(2*(dy-dx)) D+2*dy
  //   5
  //   18- CLK ON + CLR
  //   14- NXT LN + CLR
  //   02- In to GPU
  //   D > 0
  //   1 - Pulse YI
  //   2 - YI CLR
  //   3 - DY < 0 yi--
  //   4 -DY STR
  //   5 - DY < 0 invert
  //   6 - D IN
  //   7 - X CLR
  //   8 - X UP
  //   9 - X LD
  //   10 - PLT
  //   11 - RST screen
  //   12 - Y IN
  //   13 - Y y1/yi
  //   14 - Y sub IN
  //   15 - D sub IN
  //   16 - D sub/d2
  //   ELSE
  //   contents of rom_2 (hex, n*v repeats v):
  //   9 14 e 14 e 14 e 14 e 14 e 14 e 14 e 14 e 14 e 14 e 14 e 14 e 14 e 14 e 14 e 14 e 14 e 14 e 14 e 14
  //   e 14 e 14 e 14 e 14 e 14 e 14 e 14 e 14 e 14 e 14 e 14 e 14 e 14 e 14 e 14 e 14 e 14 e 14 e 14 e 14
  //   e 14 e 14 e 14 e 14 e 14 e 14 e 14 e 14 e 14 e 14 e 14 e 14 e 14 e 14 e 14 e 14 e 14 e 14 e 14 e 14
  //   e 14 e 14 e 14 e 14 e 14 e 14 e 14 e 14 e 14 e 14 e 14 e 14 e 14 e 14 e 14 e 14 e 14 e 14 e 14 e 14
  //   e 14 e 14 e 14 e 14 e 14 e 14 e 14 e 14 e 14 e 14 e 14 e 14 e 14 e 14 e 14 e 14
  //   contents of rom_3 (hex, n*v repeats v):
  //   6c62 1 4 0 4 18 20 4000 800 2000 180 200 1800 2000 8020 18020 4000 80 200 1800 2000 8020 18020 4000
  //   80 200 1800 2000 8020 18020 4000 80 200 1800 2000 8020 18020 4000 80 200 1800 2000 8020 18020 4000
  //   80 200 1800 2000 8020 18020 4000 80 200 1800 2000 8020 18020 4000 80 200 1800 2000 8020 18020 4000
  //   80 200 1800 2000 8020 18020 4000 80 200 1800 2000 8020 18020 4000 80 200 1800 2000 8020 18020 4000
  //   80 200 1800 2000 8020 18020 4000 80 200 1800 2000 8020 18020 4000 80 200 1800 2000 8020 18020 4000
  //   80 200 1800 2000 8020 18020 4000 80 200 1800 2000 8020 18020 4000 80 200 1800 2000 8020 18020 4000
  //   80 200 1800 2000 8020 18020 4000 80 200 1800 2000 8020 18020 4000 80 200 1800 2000 8020 18020 4000
  //   80 200 1800 2000 8020 18020 4000 80 200 1800 2000 8020 18020 4000 80 200 1800 2000 8020 18020 4000
  //   80 200 1800 2000 8020 18020 4000 80 200 1800 2000 8020 18020 4000 80 200 1800 2000 8020 18020 4000
  //   80 200 1800 2000 8020 18020 4000 80 200 1800 2000 8020 18020 4000 80 200 1800 2000 8020 18020 4000
  //   80 200 1800 2000 8020 18020 4000 80 200 1800 2000 8020 18020 4000 80 200 1800 2000 8020 18020 4000
  //   80 200 1800 2000 8020 18020 4000 80 200 1800 2000 8020 18020 4000 80 200 1800 2000 8020 18020 4000
  //   80 200 1800 2000 8020 18020 4000 80 200 1800 2000 8020 18020 4000 80 200 1800 2000 8020 18020 4000
  //   80 200 1800 2000 8020 18020 4000 80 200 1800 2000 8020 18020 4000 80 200 1800 2000 8020 18020 4000
  //   80 200 1800 2000 8020 18020 4000 80 200 1800 2000 8020 18020 4000 80 200 1800 2000 8020 18020 4000
  //   80 200 1800 2000 8020 18020 4000 80 200 1800 2000 8020 18020 4000 80 200 1800 2000 8020 18020 4000
  //   80 200 1800 2000 8020 18020 4000 80 200 1800 2000 8020 18020 4000 80 200 1800 2000 8020 18020 4000
  //   80 200 1800 2000 8020 18020 4000 80 200 1800 2000 8020 18020 4000 80 200 1800 2000 8020 18020 4000
  //   80 200 1800 2000 8020 18020 4000 80 200 1800 2000 8020 18020 4000 80 200 1800 2000 8020 18020 4000
  //   80 200 1800 2000 8020 18020 4000 80 200 1800 2000 8020 18020 4000 80 200 1800 2000 8020 18020 4000
  //   80 200 1800 2000 8020 18020 4000 80 200 1800 2000 8020 18020 4000 80 200 1800 2000 8020 18020 4000
  //   80 200 1800 2000 8020 18020 4000 80 200 1800 2000 8020 18020 4000 80 200 1800 2000 8020 18020 4000
  //   80 200 1800 2000 8020 18020 4000 80 200 1800 2000 8020 18020 4000 80 200 1800 2000 8020 18020 4000
  //   80 200 1800 2000 8020 18020 4000 80 200 1800 2000 8020 18020 4000 80
endmodule

module multicore (
);

  wire and_1_out, and_2_out, and_3_out, and_4_out, and_5_out, and_6_out, and_7_out, and_8_out, and_9_out,
       and_10_out, and_11_out, and_12_out, and_13_out, and_14_out, and_15_out, and_16_out, and_17_out,
       and_18_out, and_19_out, and_20_out, and_21_out, and_22_out, and_23_out, and_24_out, and_25_out,
       and_26_out, and_27_out, and_28_out, and_29_out, and_30_out, and_31_out, and_32_out, comparator_1_eq,
       comparator_1_gt, comparator_2_eq, comparator_2_lt, comparator_3_eq, comparator_3_gt, comparator_4_eq,
       comparator_4_lt, comparator_5_eq, comparator_5_gt, comparator_6_eq, comparator_6_lt, comparator_7_eq,
       comparator_7_gt, comparator_8_eq, comparator_8_lt, comparator_9_eq, comparator_9_gt, comparator_10_eq,
       comparator_10_lt, comparator_11_eq, comparator_11_gt, comparator_12_eq, comparator_12_lt,
       comparator_13_eq, comparator_13_gt, comparator_14_eq, comparator_14_lt, comparator_15_eq,
       comparator_15_gt, comparator_16_eq, comparator_16_lt, comparator_17_eq, comparator_17_gt,
       comparator_18_eq, comparator_18_lt, comparator_19_eq, comparator_19_gt, comparator_20_eq,
       comparator_20_lt, comparator_21_eq, comparator_21_gt, comparator_22_eq, comparator_22_lt,
       comparator_23_eq, comparator_23_gt, comparator_24_eq, comparator_24_lt, comparator_25_eq,
       comparator_25_gt, comparator_26_eq, comparator_26_lt, comparator_27_eq, comparator_27_gt,
       comparator_28_eq, comparator_28_lt, comparator_29_eq, comparator_29_gt, comparator_30_eq,
       comparator_30_lt, comparator_31_eq, comparator_31_gt, comparator_32_eq, comparator_32_lt,
       comparator_33_eq, comparator_33_gt, comparator_34_eq, comparator_34_lt, comparator_35_eq,
       comparator_35_gt, comparator_36_eq, comparator_36_lt, comparator_37_eq, comparator_37_gt,
       comparator_38_eq, comparator_38_lt, comparator_39_eq, comparator_39_gt, comparator_40_eq,
       comparator_40_lt, comparator_41_eq, comparator_41_gt, comparator_42_eq, comparator_42_lt,
       comparator_43_eq, comparator_43_gt, comparator_44_eq, comparator_44_lt, comparator_45_eq,
       comparator_45_gt, comparator_46_eq, comparator_46_lt, comparator_47_eq, comparator_47_gt,
       comparator_48_eq, comparator_48_lt, comparator_49_eq, comparator_49_gt, comparator_50_eq,
       comparator_50_lt, comparator_51_eq, comparator_51_gt, comparator_52_eq, comparator_52_lt,
       comparator_53_eq, comparator_53_gt, comparator_54_eq, comparator_54_lt, comparator_55_eq,
       comparator_55_gt, comparator_56_eq, comparator_56_lt, comparator_57_eq, comparator_57_gt,
       comparator_58_eq, comparator_58_lt, comparator_59_eq, comparator_59_gt, comparator_60_eq,
       comparator_60_lt, comparator_61_eq, comparator_61_gt, comparator_62_eq, comparator_62_lt,
       comparator_63_eq, comparator_63_gt, comparator_64_eq, comparator_64_lt, dipswitch_1_sw1, Lines_clk,
       Lines_finished, Lines_we, or_1_out, or_2_out, or_3_out, or_4_out, or_5_out, or_6_out, or_7_out,
       or_8_out, or_9_out, or_10_out, or_11_out, or_12_out, or_13_out, or_14_out, or_15_out, or_16_out,
       or_17_out, or_18_out, or_19_out, or_20_out, or_21_out, or_22_out, or_23_out, or_24_out, or_25_out,
       or_26_out, or_27_out, or_28_out, or_29_out, or_30_out, or_31_out, or_32_out, or_33_out, or_34_out,
       or_35_out, or_36_out, or_37_out, or_38_out, or_39_out, or_40_out, or_41_out, or_42_out, or_43_out,
       or_44_out, or_45_out, or_46_out, or_47_out, or_48_out, or_49_out, or_50_out, or_51_out, or_52_out,
       or_53_out, or_54_out, or_55_out, or_56_out, or_57_out, or_58_out, or_59_out, or_60_out, or_61_out,
       or_62_out, or_63_out, or_64_out, rgb_video_1_p1, undriven;
  wire [5:0] Light_X_sw1, Light_Y_sw1, Lines_x_out, Lines_y_out;
  wire [7:0] Lines_ln_cnt, SQRT_data;
  wire [12:0] adder_1_out, multiplier_1_out, multiplier_2_out, subtractor_1_out, subtractor_2_out;
  wire [23:0] adder_2_out, multiplexer_2_out, rgb_video_1_p6;
  wire [47:0] rom_2_data, rom_3_data;

  ROM #(.dataWidth(1)) rom_1 (.addr(Lines_ln_cnt));  // open: data
  ROM #(.dataWidth(48)) rom_2 (.addr(Lines_ln_cnt), .data(rom_2_data));
  ROM #(.dataWidth(48)) rom_3 (.addr(Lines_ln_cnt), .data(rom_3_data));
  singlecore Lines (
    .A_IN(rom_2_data), .B_IN(rom_3_data), .STR(dipswitch_1_sw1), .RST(rgb_video_1_p1), .FOV(16'h100),
    .LN_CNT(Lines_ln_cnt), .Finished(Lines_finished), .CLK(Lines_clk), .WE(Lines_we), .X_OUT(Lines_x_out),
    .Y_OUT(Lines_y_out));  // open: RST_OUT, RGB
  // RGB_Video #(.cursor("No Cursor"), .height(64), .scale(8), .width(64)) rgb_video_1: pin names not known; wires that end beside it: rgb_video_1_p1, Lines_clk, Lines_we, Lines_x_out, Lines_y_out, rgb_video_1_p6
  Subtractor #(.width(13)) subtractor_1 (
    .a({{7{1'b0}}, Lines_x_out}), .b({{7{1'b0}}, Light_X_sw1}), .out(subtractor_1_out));  // open: bin, bout
  Subtractor #(.width(13)) subtractor_2 (
    .a({{7{1'b0}}, Lines_y_out}), .b({{7{1'b0}}, Light_Y_sw1}), .out(subtractor_2_out));  // open: bin, bout
  Multiplexer #(.width(24)) multiplexer_1 (
    .in0(multiplexer_2_out), .in1(adder_2_out), .out(rgb_video_1_p6), .sel(undriven));
  Multiplier #(.width(13)) multiplier_1 (
    .a(subtractor_1_out), .b(subtractor_1_out), .out(multiplier_1_out));  // open: cin, cout
  Multiplier #(.width(13)) multiplier_2 (
    .a(subtractor_2_out), .b(subtractor_2_out), .out(multiplier_2_out));  // open: cin, cout
  Adder #(.width(13)) adder_1 (.a(multiplier_1_out), .b(multiplier_2_out), .out(adder_1_out));  // open: cin, cout
  Adder #(.width(24)) adder_2 (.a(multiplexer_2_out), .b(24'hdddddd), .out(adder_2_out));  // open: cin, cout
  Button RST (.out(rgb_video_1_p1));
  DipSwitch #(.number(5)) dipswitch_1 (.sw1(dipswitch_1_sw1));  // open: sw2, sw3, sw4, sw5
  LED led_1 (.in(Lines_finished));
  DipSwitch #(.number(6)) Light_X (
    .sw1(Light_X_sw1[0]), .sw2(Light_X_sw1[1]), .sw3(Light_X_sw1[2]), .sw4(Light_X_sw1[3]),
    .sw5(Light_X_sw1[4]), .sw6(Light_X_sw1[5]));
  ROM #(.addrWidth(13)) SQRT (.addr(adder_1_out), .data(SQRT_data));
  DipSwitch #(.number(6)) Light_Y (
    .sw1(Light_Y_sw1[0]), .sw2(Light_Y_sw1[1]), .sw3(Light_Y_sw1[2]), .sw4(Light_Y_sw1[3]),
    .sw5(Light_Y_sw1[4]), .sw6(Light_Y_sw1[5]));
  Comparator comparator_1 (.a(SQRT_data), .b({8{1'b0}}), .gt(comparator_1_gt), .eq(comparator_1_eq));  // open: lt
  Comparator comparator_2 (.a(SQRT_data), .b(8'h2), .eq(comparator_2_eq), .lt(comparator_2_lt));  // open: gt
  or or_1 (or_1_out, comparator_1_gt, comparator_1_eq);
  and and_1 (and_1_out, or_1_out, or_2_out);
  or or_2 (or_2_out, comparator_2_eq, comparator_2_lt);
  or or_3 (or_3_out, comparator_3_gt, comparator_3_eq);
  Comparator comparator_3 (.a(SQRT_data), .b(8'hc), .gt(comparator_3_gt), .eq(comparator_3_eq));  // open: lt
  or or_4 (or_4_out, comparator_4_eq, comparator_4_lt);
  Comparator comparator_4 (.a(SQRT_data), .b(8'he), .eq(comparator_4_eq), .lt(comparator_4_lt));  // open: gt
  or or_5 (or_5_out, comparator_5_gt, comparator_5_eq);
  Comparator comparator_5 (.a(SQRT_data), .b(8'h1d), .gt(comparator_5_gt), .eq(comparator_5_eq));  // open: lt
  or or_6 (or_6_out, comparator_6_eq, comparator_6_lt);
  Comparator comparator_6 (.a(SQRT_data), .b(8'h1f), .eq(comparator_6_eq), .lt(comparator_6_lt));  // open: gt
  or or_7 (or_7_out, comparator_7_gt, comparator_7_eq);
  Comparator comparator_7 (.a(SQRT_data), .b(8'h2f), .gt(comparator_7_gt), .eq(comparator_7_eq));  // open: lt
  or or_8 (or_8_out, comparator_8_eq, comparator_8_lt);
  Comparator comparator_8 (.a(SQRT_data), .b(8'h31), .eq(comparator_8_eq), .lt(comparator_8_lt));  // open: gt
  Comparator comparator_9 (.a(SQRT_data), .b(8'h41), .gt(comparator_9_gt), .eq(comparator_9_eq));  // open: lt
  Comparator comparator_10 (.a(SQRT_data), .b(8'h43), .eq(comparator_10_eq), .lt(comparator_10_lt));  // open: gt
  Comparator comparator_11 (.a(SQRT_data), .b(8'h53), .gt(comparator_11_gt), .eq(comparator_11_eq));  // open: lt
  Comparator comparator_12 (.a(SQRT_data), .b(8'h55), .eq(comparator_12_eq), .lt(comparator_12_lt));  // open: gt
  Multiplexer #(.width(24)) multiplexer_2 (.in1({24{1'b1}}), .out(multiplexer_2_out), .sel(and_1_out));  // open: in0
  Multiplexer #(.width(24)) multiplexer_3 (.in1(24'he5e5e5), .out(multiplexer_2_out), .sel(and_2_out));  // open: in0
  and and_2 (and_2_out, or_3_out, or_4_out);
  Multiplexer #(.width(24)) multiplexer_4 (.in1(24'hbdbdbd), .out(multiplexer_2_out), .sel(and_3_out));  // open: in0
  and and_3 (and_3_out, or_5_out, or_6_out);
  Multiplexer #(.width(24)) multiplexer_5 (.in1(24'h969696), .out(multiplexer_2_out), .sel(and_4_out));  // open: in0
  and and_4 (and_4_out, or_7_out, or_8_out);
  or or_9 (or_9_out, comparator_9_gt, comparator_9_eq);
  and and_5 (and_5_out, or_9_out, or_10_out);
  or or_10 (or_10_out, comparator_10_eq, comparator_10_lt);
  or or_11 (or_11_out, comparator_11_gt, comparator_11_eq);
  and and_6 (and_6_out, or_11_out, or_12_out);
  or or_12 (or_12_out, comparator_12_eq, comparator_12_lt);
  Multiplexer #(.width(24)) multiplexer_6 (.in1(24'h6e6e6e), .out(multiplexer_2_out), .sel(and_5_out));  // open: in0
  Multiplexer #(.width(24)) multiplexer_7 (.in1(24'h474747), .out(multiplexer_2_out), .sel(and_6_out));  // open: in0
  or or_13 (or_13_out, comparator_13_gt, comparator_13_eq);
  Comparator comparator_13 (.a(SQRT_data), .b(8'h3), .gt(comparator_13_gt), .eq(comparator_13_eq));  // open: lt
  or or_14 (or_14_out, comparator_14_eq, comparator_14_lt);
  Comparator comparator_14 (.a(SQRT_data), .b(8'h5), .eq(comparator_14_eq), .lt(comparator_14_lt));  // open: gt
  Comparator comparator_15 (.a(SQRT_data), .b(8'hf), .gt(comparator_15_gt), .eq(comparator_15_eq));  // open: lt
  Comparator comparator_16 (.a(SQRT_data), .b(8'h10), .eq(comparator_16_eq), .lt(comparator_16_lt));  // open: gt
  Comparator comparator_17 (.a(SQRT_data), .b(8'h20), .gt(comparator_17_gt), .eq(comparator_17_eq));  // open: lt
  Comparator comparator_18 (.a(SQRT_data), .b(8'h22), .eq(comparator_18_eq), .lt(comparator_18_lt));  // open: gt
  Comparator comparator_19 (.a(SQRT_data), .b(8'h32), .gt(comparator_19_gt), .eq(comparator_19_eq));  // open: lt
  Comparator comparator_20 (.a(SQRT_data), .b(8'h34), .eq(comparator_20_eq), .lt(comparator_20_lt));  // open: gt
  Comparator comparator_21 (.a(SQRT_data), .b(8'h44), .gt(comparator_21_gt), .eq(comparator_21_eq));  // open: lt
  Comparator comparator_22 (.a(SQRT_data), .b(8'h46), .eq(comparator_22_eq), .lt(comparator_22_lt));  // open: gt
  Comparator comparator_23 (.a(SQRT_data), .b(8'h56), .gt(comparator_23_gt), .eq(comparator_23_eq));  // open: lt
  Comparator comparator_24 (.a(SQRT_data), .b(8'h58), .eq(comparator_24_eq), .lt(comparator_24_lt));  // open: gt
  Multiplexer #(.width(24)) multiplexer_8 (.in1(24'hf8f8f8), .out(multiplexer_2_out), .sel(and_7_out));  // open: in0
  and and_7 (and_7_out, or_13_out, or_14_out);
  or or_15 (or_15_out, comparator_15_gt, comparator_15_eq);
  and and_8 (and_8_out, or_15_out, or_16_out);
  or or_16 (or_16_out, comparator_16_eq, comparator_16_lt);
  or or_17 (or_17_out, comparator_17_gt, comparator_17_eq);
  and and_9 (and_9_out, or_17_out, or_18_out);
  or or_18 (or_18_out, comparator_18_eq, comparator_18_lt);
  or or_19 (or_19_out, comparator_19_gt, comparator_19_eq);
  and and_10 (and_10_out, or_19_out, or_20_out);
  or or_20 (or_20_out, comparator_20_eq, comparator_20_lt);
  or or_21 (or_21_out, comparator_21_gt, comparator_21_eq);
  and and_11 (and_11_out, or_21_out, or_22_out);
  or or_22 (or_22_out, comparator_22_eq, comparator_22_lt);
  or or_23 (or_23_out, comparator_23_gt, comparator_23_eq);
  and and_12 (and_12_out, or_23_out, or_24_out);
  or or_24 (or_24_out, comparator_24_eq, comparator_24_lt);
  Multiplexer #(.width(24)) multiplexer_9 (.in1(24'hdedede), .out(multiplexer_2_out), .sel(and_8_out));  // open: in0
  Multiplexer #(.width(24)) multiplexer_10 (.in1(24'hb7b7b7), .out(multiplexer_2_out), .sel(and_9_out));  // open: in0
  Multiplexer #(.width(24)) multiplexer_11 (.in1(24'h8f8f8f), .out(multiplexer_2_out), .sel(and_10_out));  // open: in0
  Multiplexer #(.width(24)) multiplexer_12 (.in1(24'h686868), .out(multiplexer_2_out), .sel(and_11_out));  // open: in0
  Multiplexer #(.width(24)) multiplexer_13 (.in1(24'h404040), .out(multiplexer_2_out), .sel(and_12_out));  // open: in0
  Comparator comparator_25 (.a(SQRT_data), .b(8'h6), .gt(comparator_25_gt), .eq(comparator_25_eq));  // open: lt
  Comparator comparator_26 (.a(SQRT_data), .b(8'h8), .eq(comparator_26_eq), .lt(comparator_26_lt));  // open: gt
  Comparator comparator_27 (.a(SQRT_data), .b(8'h11), .gt(comparator_27_gt), .eq(comparator_27_eq));  // open: lt
  Comparator comparator_28 (.a(SQRT_data), .b(8'h13), .eq(comparator_28_eq), .lt(comparator_28_lt));  // open: gt
  or or_25 (or_25_out, comparator_25_gt, comparator_25_eq);
  and and_13 (and_13_out, or_25_out, or_26_out);
  or or_26 (or_26_out, comparator_26_eq, comparator_26_lt);
  or or_27 (or_27_out, comparator_27_gt, comparator_27_eq);
  or or_28 (or_28_out, comparator_28_eq, comparator_28_lt);
  or or_29 (or_29_out, comparator_29_gt, comparator_29_eq);
  Comparator comparator_29 (.a(SQRT_data), .b(8'h23), .gt(comparator_29_gt), .eq(comparator_29_eq));  // open: lt
  or or_30 (or_30_out, comparator_30_eq, comparator_30_lt);
  Comparator comparator_30 (.a(SQRT_data), .b(8'h25), .eq(comparator_30_eq), .lt(comparator_30_lt));  // open: gt
  or or_31 (or_31_out, comparator_31_gt, comparator_31_eq);
  Comparator comparator_31 (.a(SQRT_data), .b(8'h35), .gt(comparator_31_gt), .eq(comparator_31_eq));  // open: lt
  or or_32 (or_32_out, comparator_32_eq, comparator_32_lt);
  Comparator comparator_32 (.a(SQRT_data), .b(8'h37), .eq(comparator_32_eq), .lt(comparator_32_lt));  // open: gt
  or or_33 (or_33_out, comparator_33_gt, comparator_33_eq);
  Comparator comparator_33 (.a(SQRT_data), .b(8'h47), .gt(comparator_33_gt), .eq(comparator_33_eq));  // open: lt
  or or_34 (or_34_out, comparator_34_eq, comparator_34_lt);
  Comparator comparator_34 (.a(SQRT_data), .b(8'h49), .eq(comparator_34_eq), .lt(comparator_34_lt));  // open: gt
  or or_35 (or_35_out, comparator_35_gt, comparator_35_eq);
  Comparator comparator_35 (.a(SQRT_data), .b(8'h59), .gt(comparator_35_gt), .eq(comparator_35_eq));  // open: lt
  or or_36 (or_36_out, comparator_36_eq, comparator_36_lt);
  Comparator comparator_36 (.a(SQRT_data), .b(8'h5b), .eq(comparator_36_eq), .lt(comparator_36_lt));  // open: gt
  Multiplexer #(.width(24)) multiplexer_14 (.in1(24'hf2f2f2), .out(multiplexer_2_out), .sel(and_13_out));  // open: in0
  Multiplexer #(.width(24)) multiplexer_15 (.in1(24'hd8d8d8), .out(multiplexer_2_out), .sel(and_14_out));  // open: in0
  and and_14 (and_14_out, or_27_out, or_28_out);
  Multiplexer #(.width(24)) multiplexer_16 (.in1(24'hb0b0b0), .out(multiplexer_2_out), .sel(and_15_out));  // open: in0
  and and_15 (and_15_out, or_29_out, or_30_out);
  Multiplexer #(.width(24)) multiplexer_17 (.in1(24'h898989), .out(multiplexer_2_out), .sel(and_16_out));  // open: in0
  and and_16 (and_16_out, or_31_out, or_32_out);
  Multiplexer #(.width(24)) multiplexer_18 (.in1(24'h616161), .out(multiplexer_2_out), .sel(and_17_out));  // open: in0
  and and_17 (and_17_out, or_33_out, or_34_out);
  Multiplexer #(.width(24)) multiplexer_19 (.in1(24'h3a3a3a), .out(multiplexer_2_out), .sel(and_18_out));  // open: in0
  and and_18 (and_18_out, or_35_out, or_36_out);
  Comparator comparator_37 (.a(SQRT_data), .b(8'h9), .gt(comparator_37_gt), .eq(comparator_37_eq));  // open: lt
  Comparator comparator_38 (.a(SQRT_data), .b(8'hb), .eq(comparator_38_eq), .lt(comparator_38_lt));  // open: gt
  or or_37 (or_37_out, comparator_37_gt, comparator_37_eq);
  and and_19 (and_19_out, or_37_out, or_38_out);
  or or_38 (or_38_out, comparator_38_eq, comparator_38_lt);
  or or_39 (or_39_out, comparator_39_gt, comparator_39_eq);
  Comparator comparator_39 (.a(SQRT_data), .b(8'h14), .gt(comparator_39_gt), .eq(comparator_39_eq));  // open: lt
  or or_40 (or_40_out, comparator_40_eq, comparator_40_lt);
  Comparator comparator_40 (.a(SQRT_data), .b(8'h16), .eq(comparator_40_eq), .lt(comparator_40_lt));  // open: gt
  or or_41 (or_41_out, comparator_41_gt, comparator_41_eq);
  Comparator comparator_41 (.a(SQRT_data), .b(8'h26), .gt(comparator_41_gt), .eq(comparator_41_eq));  // open: lt
  or or_42 (or_42_out, comparator_42_eq, comparator_42_lt);
  Comparator comparator_42 (.a(SQRT_data), .b(8'h28), .eq(comparator_42_eq), .lt(comparator_42_lt));  // open: gt
  or or_43 (or_43_out, comparator_43_gt, comparator_43_eq);
  Comparator comparator_43 (.a(SQRT_data), .b(8'h38), .gt(comparator_43_gt), .eq(comparator_43_eq));  // open: lt
  or or_44 (or_44_out, comparator_44_eq, comparator_44_lt);
  Comparator comparator_44 (.a(SQRT_data), .b(8'h3a), .eq(comparator_44_eq), .lt(comparator_44_lt));  // open: gt
  Comparator comparator_45 (.a(SQRT_data), .b(8'h4a), .gt(comparator_45_gt), .eq(comparator_45_eq));  // open: lt
  Comparator comparator_46 (.a(SQRT_data), .b(8'h4c), .eq(comparator_46_eq), .lt(comparator_46_lt));  // open: gt
  Comparator comparator_47 (.a(SQRT_data), .b(8'h5c), .gt(comparator_47_gt), .eq(comparator_47_eq));  // open: lt
  Comparator comparator_48 (.a(SQRT_data), .b(8'h5e), .eq(comparator_48_eq), .lt(comparator_48_lt));  // open: gt
  Multiplexer #(.width(24)) multiplexer_20 (.in1(24'hebebeb), .out(multiplexer_2_out), .sel(and_19_out));  // open: in0
  Multiplexer #(.width(24)) multiplexer_21 (.in1(24'hd1d1d1), .out(multiplexer_2_out), .sel(and_20_out));  // open: in0
  and and_20 (and_20_out, or_39_out, or_40_out);
  Multiplexer #(.width(24)) multiplexer_22 (.in1(24'ha9a9a9), .out(multiplexer_2_out), .sel(and_21_out));  // open: in0
  and and_21 (and_21_out, or_41_out, or_42_out);
  Multiplexer #(.width(24)) multiplexer_23 (.in1(24'h828282), .out(multiplexer_2_out), .sel(and_22_out));  // open: in0
  and and_22 (and_22_out, or_43_out, or_44_out);
  or or_45 (or_45_out, comparator_45_gt, comparator_45_eq);
  and and_23 (and_23_out, or_45_out, or_46_out);
  or or_46 (or_46_out, comparator_46_eq, comparator_46_lt);
  or or_47 (or_47_out, comparator_47_gt, comparator_47_eq);
  and and_24 (and_24_out, or_47_out, or_48_out);
  or or_48 (or_48_out, comparator_48_eq, comparator_48_lt);
  Multiplexer #(.width(24)) multiplexer_24 (.in1(24'h5a5a5a), .out(multiplexer_2_out), .sel(and_23_out));  // open: in0
  Multiplexer #(.width(24)) multiplexer_25 (.in1(24'h333333), .out(multiplexer_2_out), .sel(and_24_out));  // open: in0
  Comparator comparator_49 (.a(SQRT_data), .b(8'h17), .gt(comparator_49_gt), .eq(comparator_49_eq));  // open: lt
  Comparator comparator_50 (.a(SQRT_data), .b(8'h19), .eq(comparator_50_eq), .lt(comparator_50_lt));  // open: gt
  Comparator comparator_51 (.a(SQRT_data), .b(8'h29), .gt(comparator_51_gt), .eq(comparator_51_eq));  // open: lt
  Comparator comparator_52 (.a(SQRT_data), .b(8'h2b), .eq(comparator_52_eq), .lt(comparator_52_lt));  // open: gt
  Comparator comparator_53 (.a(SQRT_data), .b(8'h3b), .gt(comparator_53_gt), .eq(comparator_53_eq));  // open: lt
  Comparator comparator_54 (.a(SQRT_data), .b(8'h3d), .eq(comparator_54_eq), .lt(comparator_54_lt));  // open: gt
  or or_49 (or_49_out, comparator_49_gt, comparator_49_eq);
  and and_25 (and_25_out, or_49_out, or_50_out);
  or or_50 (or_50_out, comparator_50_eq, comparator_50_lt);
  or or_51 (or_51_out, comparator_51_gt, comparator_51_eq);
  and and_26 (and_26_out, or_51_out, or_52_out);
  or or_52 (or_52_out, comparator_52_eq, comparator_52_lt);
  or or_53 (or_53_out, comparator_53_gt, comparator_53_eq);
  or or_54 (or_54_out, comparator_54_eq, comparator_54_lt);
  or or_55 (or_55_out, comparator_55_gt, comparator_55_eq);
  Comparator comparator_55 (.a(SQRT_data), .b(8'h4d), .gt(comparator_55_gt), .eq(comparator_55_eq));  // open: lt
  or or_56 (or_56_out, comparator_56_eq, comparator_56_lt);
  Comparator comparator_56 (.a(SQRT_data), .b(8'h4f), .eq(comparator_56_eq), .lt(comparator_56_lt));  // open: gt
  Multiplexer #(.width(24)) multiplexer_26 (.in1(24'hcacaca), .out(multiplexer_2_out), .sel(and_25_out));  // open: in0
  Multiplexer #(.width(24)) multiplexer_27 (.in1(24'ha3a3a3), .out(multiplexer_2_out), .sel(and_26_out));  // open: in0
  Multiplexer #(.width(24)) multiplexer_28 (.in1(24'h7b7b7b), .out(multiplexer_2_out), .sel(and_27_out));  // open: in0
  and and_27 (and_27_out, or_53_out, or_54_out);
  Multiplexer #(.width(24)) multiplexer_29 (.in1(24'h545454), .out(multiplexer_2_out), .sel(and_28_out));  // open: in0
  and and_28 (and_28_out, or_55_out, or_56_out);
  Comparator comparator_57 (.a(SQRT_data), .b(8'h1a), .gt(comparator_57_gt), .eq(comparator_57_eq));  // open: lt
  Comparator comparator_58 (.a(SQRT_data), .b(8'h1c), .eq(comparator_58_eq), .lt(comparator_58_lt));  // open: gt
  Comparator comparator_59 (.a(SQRT_data), .b(8'h2c), .gt(comparator_59_gt), .eq(comparator_59_eq));  // open: lt
  Comparator comparator_60 (.a(SQRT_data), .b(8'h2e), .eq(comparator_60_eq), .lt(comparator_60_lt));  // open: gt
  or or_57 (or_57_out, comparator_57_gt, comparator_57_eq);
  and and_29 (and_29_out, or_57_out, or_58_out);
  or or_58 (or_58_out, comparator_58_eq, comparator_58_lt);
  or or_59 (or_59_out, comparator_59_gt, comparator_59_eq);
  or or_60 (or_60_out, comparator_60_eq, comparator_60_lt);
  or or_61 (or_61_out, comparator_61_gt, comparator_61_eq);
  Comparator comparator_61 (.a(SQRT_data), .b(8'h3e), .gt(comparator_61_gt), .eq(comparator_61_eq));  // open: lt
  or or_62 (or_62_out, comparator_62_eq, comparator_62_lt);
  Comparator comparator_62 (.a(SQRT_data), .b(8'h40), .eq(comparator_62_eq), .lt(comparator_62_lt));  // open: gt
  or or_63 (or_63_out, comparator_63_gt, comparator_63_eq);
  Comparator comparator_63 (.a(SQRT_data), .b(8'h50), .gt(comparator_63_gt), .eq(comparator_63_eq));  // open: lt
  or or_64 (or_64_out, comparator_64_eq, comparator_64_lt);
  Comparator comparator_64 (.a(SQRT_data), .b(8'h52), .eq(comparator_64_eq), .lt(comparator_64_lt));  // open: gt
  Multiplexer #(.width(24)) multiplexer_30 (.in1(24'hc4c4c4), .out(multiplexer_2_out), .sel(and_29_out));  // open: in0
  Multiplexer #(.width(24)) multiplexer_31 (.in1(24'h9c9c9c), .out(multiplexer_2_out), .sel(and_30_out));  // open: in0
  and and_30 (and_30_out, or_59_out, or_60_out);
  Multiplexer #(.width(24)) multiplexer_32 (.in1(24'h757575), .out(multiplexer_2_out), .sel(and_31_out));  // open: in0
  and and_31 (and_31_out, or_61_out, or_62_out);
  Multiplexer #(.width(24)) multiplexer_33 (.in1(24'h4d4d4d), .out(multiplexer_2_out), .sel(and_32_out));  // open: in0
  and and_32 (and_32_out, or_63_out, or_64_out);

  // Notes on the sheet:
  //   contents of rom_1 (hex, n*v repeats v):
  //   4*1 15*0 4*1
  //   contents of rom_2 (hex, n*v repeats v):
  //   180010 180010 280009 180030 190011 1a0010 1b0010 1c000f 1d000f 1e000e 1f000e 20000d 21000d 22000c
  //   23000c 24000b 25000b 26000a 27000a 280008 280008 3f000b 280038 290009 2a0009 2b0009 2c0009 2d0009
  //   2e000a 2f000a 30000a 31000a 32000a 33000a 34000a 35000a 36000a 37000a 38000a 39000a 3a000b 3b000b
  //   3c000b 3d000b 3e000b
  //   A Points
  //   contents of rom_3 (hex, n*v repeats v):
  //   180030 280008 280038 280038 190030 1a0031 1b0031 1c0032 1d0032 1e0033 1f0033 200034 210034 220035
  //   230035 240036 250036 260037 270037 280038 3f000a 3f0036 3f0036 290038 2a0038 2b0038 2c0038 2d0038
  //   2e0037 2f0037 300037 310037 320037 330037 340037 350037 360037 370037 380037 390037 3a0036 3b0036
  //   3c0036 3d0036 3e0036
  //   B Points
  //   contents of SQRT (hex, n*v repeats v):
  //   0 1 1 4*2 6*3 8*4 10*5 12*6 14*7 16*8 18*9 20*a 22*b 24*c 26*d 28*e 30*f 32*10 34*11 36*12 38*13
  //   40*14 42*15 44*16 46*17 48*18 50*19 52*1a 54*1b 56*1c 58*1d 60*1e 62*1f 64*20 66*21 68*22 70*23
  //   72*24 74*25 76*26 78*27 80*28 82*29 84*2a 86*2b 88*2c 90*2d 92*2e 94*2f 96*30 98*31 100*32 102*33
  //   104*34 106*35 108*36 110*37 112*38 114*39 116*3a 118*3b 120*3c 122*3d 124*3e 126*3f 128*40 130*41
  //   132*42 134*43 136*44 138*45 140*46 142*47 144*48 146*49 148*4a 150*4b 152*4c 154*4d 156*4e 158*4f
  //   160*50 162*51 164*52 166*53 168*54 170*55 172*56 174*57 176*58 178*59 180*5a 5b
  //   1- Render
endmodule
